# Fritzing sketch rpm_meter (saved by Fritzing 0.9.5d)

parts:
  R1 = Resistor [tolerance=±5% resistance=20k package=THT]
  R2 = Resistor [tolerance=±5% resistance=10k package=THT]
  R3 = Resistor [tolerance=±5% resistance=10k package=THT]
  R4 = Resistor [tolerance=±5% resistance=720 package=THT]
  Компонент1 = Arduino Pro Mini (5V)
  Компонент2 = LCD1602-I2C

nets:
  N1: R1.Pin_1, R2.Pin_0, Компонент1.D2
  N2: R3.Pin_1, R4.Pin_0
  GND: Компонент1.GND, Компонент2.GND
  N3: Компонент1.A4, Компонент2.SDA
  N4: Компонент1.A5, Компонент2.SCL
  5V: Компонент1.VCC, Компонент2.VCC

notes:
  Вход счетчика
  Вход вольтметра
  Выход псевдо холостого хода

custom parts:
  LCD1602-I2C: A standard character display, usually with 2x16 characters. Comes in many colors with LCM1602 IIC attached.
